# Fritzing sketch esquema (saved by Fritzing 0.9.3b)
breadboards: 1

parts:
  S1 = H-Bridge with L298N
  M1 = DC Motor
  VCC2 = Battery block 9V
  VCC1 = 4 x AAA Battery Mount
  U2 = ESP32-38PinWide [part_number=ESP32-38PinWide]
  M3 = Dagu DGServo 9g (Top view) [part_number=RS001B]

nets:
  N1: S1.12V, VCC2.+
  GND: S1.GND, VCC2.-, U2.GND
  N2: S1.ENA, U2.GPIO19
  N3: S1.IN1, U2.GPIO18
  N4: S1.IN2, U2.GPIO5
  N5: S1.M1-01, M1.pin_1
  N6: S1.M1-02, M1.pin_2
  N7: VCC1.-, U2.GPIO11, M3.gnd
  VIN: VCC1.+, U2.VIN, M3.vcc
  N8: U2.GPIO14, M3.pulse

custom parts:
  H-Bridge with L298N: h-bridge
  ESP32-38PinWide: Generic 38-Pin ESP32 with wide format (only access to one side of pins on a breadboard) based on Stephen Lilley's HiLetgo ESP-WROOM-32 ESP32 ESP-32S Development Board.
